# Fritzing sketch Photocell2 (saved by Fritzing 0.9.4)
breadboards: 1

parts:
  R1 = PHOTOCELL [package=photocell]
  LED1 = LED - 5mm [color="Green (560nm)" package="5 mm [THT]"]
  Part1 = Arduino Uno (Rev3)
  R2 = Resistor [tolerance=±5% resistance=10k package=THT]

nets:
  N1: R1.P$1, Part1.A0, R2.Pin_1
  N2: R1.P$2, Part1.5V
  N3: LED1.cathode, Part1.GND, R2.Pin_0
  N4: LED1.anode, Part1.D13/SCK
